# Fritzing sketch led (saved by Fritzing 0.9.4)
circuit board: 5.22219cm x 3.13981cm
breadboards: 1

parts:
  Raspberry_Pi_1 = Raspberry Pi 3 [part_number=RPI-3-V1.2]
  LED2 = LED - 5mm [color="Green (565nm)" package="5 mm [THT]"]
  LED3 = LED - 5mm [color="Blue (430nm)" package="5 mm [THT]"]
  LED1 = LED - 5mm [color="Red (633nm)" package="5 mm [THT]"]
  R3 = Resistor [tolerance=±5% resistance=10k package=THT]
  R2 = Resistor [tolerance=±5% resistance=10k package=THT]
  R1 = Resistor [tolerance=±5% resistance=10k package=THT]

nets:
  N1: Raspberry_Pi_1.GIPO21, LED1.anode
  N2: Raspberry_Pi_1.GIPO20, LED2.anode
  N3: Raspberry_Pi_1.GIPO16, LED3.anode
  N4: Raspberry_Pi_1.GND, R3.Pin_1, R2.Pin_1, R1.Pin_1
  N5: LED2.cathode, R2.Pin_0
  N6: LED3.cathode, R3.Pin_0
  N7: LED1.cathode, R1.Pin_0
